# Fritzing sketch Obstacle (saved by Fritzing 0.9.4)

parts:
  S1 = H-Bridge with L298N
  Part1 = Arduino Uno (Rev3) - ICSP
  M1 = DC Motor
  M2 = DC Motor
  BAT1 = Battery Holders [package=lipo-1100mAh]
  S3 = Round Pushbutton
  HC-SR04_Sensor_1 = HC-SR04 Ultrasonic Distance Sensor
  J1 = Basic Servo

nets:
  N1: S1.12V, S3.leg1
  N2: S1.GND, BAT1.-
  5V: S1.5V, Part1.5V
  N3: S1.ENA, Part1.D5_PWM
  N4: S1.IN1, Part1.D6_PWM
  N5: S1.IN2, Part1.D7
  N6: S1.IN3, Part1.D8
  N7: S1.IN4, Part1.D9_PWM
  N8: S1.ENB, Part1.D3_PWM
  N9: S1.M1-01, M2.pin_2
  N10: S1.M1-02, M2.pin_1
  N11: S1.M2-01, M1.pin_1
  N12: S1.M2-02, M1.pin_2
  N13: Part1.D11_PWM/MOSI, J1.pulse
  N14: Part1.D12/MISO, HC-SR04_Sensor_1.ECHO
  N15: Part1.D13/SCK, HC-SR04_Sensor_1.TRIG
  N16: BAT1.+, S3.leg0

custom parts:
  H-Bridge with L298N: h-bridge
